// Logisim project MIPS-PC.circ as structural Verilog: 6 circuits, main circuit main
module main (
  output [7:0] out_1,
  output [7:0] out_2,
  output [7:0] Rs,
  output [7:0] out_4,
  output [19:0] out_5
);

  wire ALU_zero, branchmodule_1_branchtaken, clock_1_out, controlunit_1_alusrc, controlunit_1_brancheq,
       controlunit_1_branchne, controlunit_1_jump, controlunit_1_memread, controlunit_1_memtoreg,
       controlunit_1_memwrite, controlunit_1_regdst, controlunit_1_regwrite, controlunit_1_shift;
  wire [3:0] controlunit_1_aluop, multiplexer_1_out;
  wire [7:0] adder_1_out, adder_2_out, ALU_aluoutput, bit_extender_1_out, Memory_read_data,
       multiplexer_2_out, multiplexer_3_out, multiplexer_4_out, multiplexer_5_out, multiplexer_6_out;

  Clock clock_1 (.out(clock_1_out));
  Register #(.trigger("falling")) register_1 (.D(multiplexer_6_out), .Q(Rs), .clk(clock_1_out));  // open: en, clr
  Adder adder_1 (.a(Rs), .b(8'h1), .out(adder_1_out));  // open: cin, cout
  ROM #(.dataWidth(20)) rom_1 (.addr(Rs), .data({out_5[19:16], out_2, out_5[7:0]}));  // open: sel
  ControlUnit controlunit_1 (
    .OPcode(out_5[19:16]), .BranchNE(controlunit_1_branchne), .Shift(controlunit_1_shift),
    .MemtoReg(controlunit_1_memtoreg), .RegDst(controlunit_1_regdst), .Jump(controlunit_1_jump),
    .MemWrite(controlunit_1_memwrite), .MemRead(controlunit_1_memread), .BranchEQ(controlunit_1_brancheq),
    .ALUSrc(controlunit_1_alusrc), .RegWrite(controlunit_1_regwrite), .ALUop(controlunit_1_aluop));
  Multiplexer #(.width(4), .enable("false")) multiplexer_1 (
    .in0(out_2[3:0]), .in1(out_5[7:4]), .out(multiplexer_1_out), .sel(controlunit_1_regdst));
  assign bit_extender_1_out = {{4{out_5[3]}}, out_5[3:0]};  // Bit_Extender bit_extender_1
  RegisterFile Registers (
    .Rs(out_2[7:4]), .in_2(clock_1_out), .Rt(out_2[3:0]), .Rd(multiplexer_1_out),
    .WriteData(multiplexer_5_out), .RegWrite(controlunit_1_regwrite), .Read_Data_1(out_1), .Read_Data_2(out_4));
  Multiplexer #(.width(8), .enable("false")) multiplexer_2 (
    .in0(out_1), .in1(bit_extender_1_out), .out(multiplexer_2_out), .sel(controlunit_1_shift));
  Adder adder_2 (.a(adder_1_out), .b(out_5[7:0]), .out(adder_2_out));  // open: cin, cout
  MyALU ALU (
    .AluInput1(multiplexer_2_out), .AluInput2(multiplexer_3_out), .AluOp(controlunit_1_aluop),
    .Zero(ALU_zero), .AluOutput(ALU_aluoutput));
  Multiplexer #(.width(8), .enable("false")) multiplexer_3 (
    .in0(out_4), .in1(out_5[7:0]), .out(multiplexer_3_out), .sel(controlunit_1_alusrc));
  BranchModule branchmodule_1 (
    .BranchEQ(controlunit_1_brancheq), .zero(ALU_zero), .BranchNE(controlunit_1_branchne),
    .BranchTaken(branchmodule_1_branchtaken));
  Multiplexer #(.width(8), .enable("false")) multiplexer_4 (
    .in0(adder_1_out), .in1(adder_2_out), .out(multiplexer_4_out), .sel(branchmodule_1_branchtaken));
  DataMemory Memory (
    .MemWrite(controlunit_1_memwrite), .Adress(ALU_aluoutput), .Data(out_4), .in_4(clock_1_out),
    .MemRead(controlunit_1_memread), .Read_Data(Memory_read_data));
  Multiplexer #(.width(8), .enable("false")) multiplexer_5 (
    .in0(Memory_read_data), .in1(ALU_aluoutput), .out(multiplexer_5_out), .sel(controlunit_1_memtoreg));
  Multiplexer #(.width(8), .enable("false")) multiplexer_6 (
    .in0(multiplexer_4_out), .in1(out_2), .out(multiplexer_6_out), .sel(controlunit_1_jump));

  assign out_5[15:8] = out_2;

  // Notes on the sheet:
  //   contents of rom_1 (hex, n*v repeats v):
  //   60305 60203 e2300 52400
  //   RegDst
  //   Shift
  //   AluSrc
  //   Branch
  //   Mem2Reg
endmodule

module ControlUnit (
  input  [3:0] OPcode,
  output BranchNE,
  output Shift,
  output MemtoReg,
  output RegDst,
  output Jump,
  output MemWrite,
  output MemRead,
  output BranchEQ,
  output ALUSrc,
  output RegWrite,
  output [3:0] ALUop
);

  ROM #(.addrWidth(4), .dataWidth(14)) rom_1 (
    .addr(OPcode),
    .data({ALUop, RegWrite, ALUSrc, BranchEQ, MemRead, MemWrite, Jump, RegDst, MemtoReg, Shift, BranchNE}));  // open: sel

  // Notes on the sheet:
  //   contents of rom_1 (hex, n*v repeats v):
  //   1a0c 1b04 20c 304 60c b40 b04 180d a0c 260e 704 220e 320c 1c 92c 188c
endmodule

module RegisterFile (
  input  [3:0] Rs,
  input  in_2,
  input  [3:0] Rt,
  input  [3:0] Rd,
  input  [7:0] WriteData,
  input  RegWrite,
  output [7:0] Read_Data_1,
  output [7:0] Read_Data_2
);

  wire [5:0] and_1_out, bit_extender_1_out, decoder_1_out1;
  wire [7:0] multiplexer_1_out, multiplexer_2_out, multiplexer_3_out, multiplexer_4_out, multiplexer_5_out,
       multiplexer_6_out, sp_q, t0_q, t1_q, t2_q, t3_q, t4_q, zero_q;

  Decoder #(.select(4), .enable("false")) decoder_1 (
    .out1(decoder_1_out1[0]), .out2(decoder_1_out1[1]), .out3(decoder_1_out1[2]), .out4(decoder_1_out1[3]),
    .out5(decoder_1_out1[4]), .out6(decoder_1_out1[5]), .sel(Rd));  // open: out0, out7, out8, out9, out10, out11, out12, out13, out14, out15
  assign bit_extender_1_out = {{5{RegWrite}}, RegWrite};  // Bit_Extender bit_extender_1
  assign and_1_out = decoder_1_out1 & bit_extender_1_out;  // AND_Gate and_1, 6 bits wide
  Multiplexer #(.width(8), .enable("false")) multiplexer_1 (
    .in0(t0_q), .in1(WriteData), .out(multiplexer_1_out), .sel(and_1_out[0]));
  Multiplexer #(.width(8), .enable("false")) multiplexer_2 (
    .in0(t1_q), .in1(WriteData), .out(multiplexer_2_out), .sel(and_1_out[1]));
  Multiplexer #(.width(8), .enable("false")) multiplexer_3 (
    .in0(t2_q), .in1(WriteData), .out(multiplexer_3_out), .sel(and_1_out[2]));
  Register zero (.D({8{1'b0}}), .Q(zero_q), .clk(in_2));  // open: en, clr
  Register t0 (.D(multiplexer_1_out), .Q(t0_q), .clk(in_2));  // open: en, clr
  Register t1 (.D(multiplexer_2_out), .Q(t1_q), .clk(in_2));  // open: en, clr
  Register t2 (.D(multiplexer_3_out), .Q(t2_q), .clk(in_2));  // open: en, clr
  Multiplexer #(.width(8), .enable("false")) multiplexer_4 (
    .in0(t3_q), .in1(WriteData), .out(multiplexer_4_out), .sel(and_1_out[3]));
  Multiplexer #(.width(8), .enable("false")) multiplexer_5 (
    .in0(t4_q), .in1(WriteData), .out(multiplexer_5_out), .sel(and_1_out[4]));
  Multiplexer #(.width(8), .enable("false")) multiplexer_6 (
    .in0(sp_q), .in1(WriteData), .out(multiplexer_6_out), .sel(and_1_out[5]));
  Register t3 (.D(multiplexer_4_out), .Q(t3_q), .clk(in_2));  // open: en, clr
  Register t4 (.D(multiplexer_5_out), .Q(t4_q), .clk(in_2));  // open: en, clr
  Register sp (.D(multiplexer_6_out), .Q(sp_q), .clk(in_2));  // open: en, clr
  Multiplexer #(.select(4), .width(8), .enable("false")) multiplexer_7 (
    .in0(zero_q), .in1(t0_q), .in2(t1_q), .in3(t2_q), .in4(t3_q), .in5(t4_q), .in6(sp_q), .out(Read_Data_1),
    .sel(Rs));  // open: in7, in8, in9, in10, in11, in12, in13, in14, in15
  Multiplexer #(.select(4), .width(8), .enable("false")) multiplexer_8 (
    .in0(zero_q), .in1(t0_q), .in2(t1_q), .in3(t2_q), .in4(t3_q), .in5(t4_q), .in6(sp_q), .out(Read_Data_2),
    .sel(Rt));  // open: in7, in8, in9, in10, in11, in12, in13, in14, in15
endmodule

module MyALU (
  input  [7:0] AluInput1,
  input  [7:0] AluInput2,
  input  [3:0] AluOp,
  output Zero,
  output [7:0] AluOutput
);

  wire [31:0] bit_extender_1_out, bit_extender_2_out;
  wire [31:8] mips_alu_1_p5;

  assign bit_extender_1_out = {{24{1'b0}}, AluInput1};  // Bit_Extender bit_extender_1
  assign bit_extender_2_out = {{24{1'b0}}, AluInput2};  // Bit_Extender bit_extender_2
  // MIPS_ALU mips_alu_1: pin names not known; wires that end beside it: bit_extender_1_out, bit_extender_2_out, AluOp, Zero, {mips_alu_1_p5, AluOutput}
endmodule

module DataMemory (
  input  MemWrite,
  input  [7:0] Adress,
  input  [7:0] Data,
  input  in_4,
  input  MemRead,
  output [7:0] Read_Data
);

  RAM #(.bus("separate")) ram_1 (
    .addr(Adress), .din(Data), .data(Read_Data), .str(MemWrite), .clk(in_4), .ld(MemRead));  // open: sel, clr
endmodule

module BranchModule (
  input  BranchEQ,
  input  zero,
  input  BranchNE,
  output BranchTaken
);

  wire and_1_out, and_2_out, not_1_out;

  not not_1 (not_1_out, zero);
  and and_1 (and_1_out, BranchEQ, zero);
  and and_2 (and_2_out, not_1_out, BranchNE);
  or or_1 (BranchTaken, and_1_out, and_2_out);
endmodule
